# Fritzing sketch Circuito_Acionamento_Rele (saved by Fritzing 0.9.3b)
breadboards: 1

parts:
  U1 = Optocoupler [package=THT]
  R3 = Resistor [tolerance=±5% resistance=220 package="2010 [SMD]"]
  Raspberry_Pi_1 = Raspberry Pi 3 [part_number=RPI-3-V1.2]
  R4 = Resistor [tolerance=±5% resistance=220 package="2010 [SMD]"]
  R5 = Resistor [tolerance=±5% resistance=220 package="2010 [SMD]"]
  Q1 = NPN-Transistor [package="TO92 [THT]"]
  D1 = Diode [package=diode-1n4001]
  U2 = RELAY-SOLIDSTATE [package=relay-s108t02]

nets:
  N1: U1.Pin_1, R3.Pin_0
  N2: U1.Pin_2, Raspberry_Pi_1.GND
  N3: U1.Pin_4, R4.Pin_0, R5.Pin_1
  N4: U1.Pin_5, Raspberry_Pi_1.5V, U2.-
  N5: R3.Pin_1, Raspberry_Pi_1.GPIO22
  N6: R4.Pin_1, Q1.B
  N7: R5.Pin_0, Q1.E
  N8: Q1.C, D1.C, U2.+
