# Fritzing sketch 3_Sensor_Conection_MLX90614 (saved by Fritzing 0.9.3b)
circuit board: 8.46667cm x 5.64444cm

parts:
  U1 = MLX90614 [package=to-39]
  U2 = MLX90614 [package=to-39]
  U3 = MLX90614 [package=to-39]
  J2 = female pin header, 4 pins [form="♀ (female)"]
  Raspberry_Pi_3_b_+ = Raspberry Pi B+
  U4 = MLX90614 [package=to-39]

nets:
  N1: U1.SCL_VZ, U2.SCL_VZ, U3.SCL_VZ, J2.pin3, Raspberry_Pi_3_b_+.GPIO3, U4.SCL_VZ
  N2: U1.PWM_SDA, U2.PWM_SDA, U3.PWM_SDA, J2.pin4, Raspberry_Pi_3_b_+.GPIO2, U4.PWM_SDA
  VDD: U1.VDD, U2.VDD, U3.VDD, J2.pin1, Raspberry_Pi_3_b_+.3v3, Raspberry_Pi_3_b_+.3V3, U4.VDD
  VSS: U1.VSS, U2.VSS, U3.VSS, J2.pin2, Raspberry_Pi_3_b_+.GND, U4.VSS
