# Fritzing sketch Esquematico_Conec_Sistema_Aquisicao (saved by Fritzing 0.9.3b)
circuit board: 8.46667cm x 5.64444cm

parts:
  YF-S201_Flow_Meter1 = YF-S201 Water Flow Meter
  YF-S201_Flow_Meter2 = YF-S201 Water Flow Meter
  YF-S201_Flow_Meter3 = YF-S201 Water Flow Meter
  Raspberry_Pi1 = Raspberry Pi B+
  U1 = MLX90614 [package=to-39]
  J2 = female pin header, 4 pins [form="♀ (female)"]
  U3 = MLX90614 [package=to-39]
  U2 = MLX90614 [package=to-39]

nets:
  N1: YF-S201_Flow_Meter1.SIG, YF-S201_Flow_Meter2.SIG, YF-S201_Flow_Meter3.SIG, Raspberry_Pi1.GPIO27
  GND: YF-S201_Flow_Meter1.GND, YF-S201_Flow_Meter2.GND, YF-S201_Flow_Meter3.GND, Raspberry_Pi1.GND, U1.VSS, J2.pin2, U3.VSS, U2.VSS
  VCC: YF-S201_Flow_Meter1.VCC, YF-S201_Flow_Meter2.VCC, YF-S201_Flow_Meter3.VCC, Raspberry_Pi1.5V
  VDD: Raspberry_Pi1.3v3, U1.VDD, J2.pin1, U3.VDD, U2.VDD
  N2: Raspberry_Pi1.GPIO2, U1.PWM_SDA, J2.pin4, U3.PWM_SDA, U2.PWM_SDA
  N3: Raspberry_Pi1.GPIO3, U1.SCL_VZ, J2.pin3, U3.SCL_VZ, U2.SCL_VZ

custom parts:
  YF-S201 Water Flow Meter: The YF-S201 Flow Meter. The input voltage is 5V to 24V (DC).
