# Fritzing sketch Fonte_reguladora_peltier (saved by Fritzing 0.9.3b)
breadboards: 1

parts:
  U1 = Transformer [package=transformer]
  C1 = Electrolytic Capacitor [capacitance=1µF package="100 mil [THT, electrolytic]"]
  R1 = Resistor [tolerance=±5% resistance=220 package="0402 [SMD]"]
  D1 = Rectifier Diode [part_number=1N4001 package="Melf DO-213 AB [SMD]"]
  U2 = DIODE-ZENER [package=diode-zener]
  Q1 = NPN-Transistor [package="TO92 [THT]"]
  D2 = Rectifier Diode [part_number=1N4001 package="Melf DO-213 AB [SMD]"]
  D3 = Rectifier Diode [part_number=1N4001 package="Melf DO-213 AB [SMD]"]
  D4 = Rectifier Diode [part_number=1N4001 package="Melf DO-213 AB [SMD]"]  # not connected
  C2 = Electrolytic Capacitor [capacitance=1µF package="100 mil [THT, electrolytic]"]
  C3 = Electrolytic Capacitor [capacitance=1µF package="100 mil [THT, electrolytic]"]
  C4 = Electrolytic Capacitor [capacitance=1µF package="100 mil [THT, electrolytic]"]
  J1 = Peltier Element

nets:
  N1: U1.3, D2.anode
  N2: U1.4, D1.anode, D3.cathode
  N3: C1.-, D3.anode, C2.-, C3.-, C4.-, J1.pin1
  N4: C1.+, R1.Pin_0, D1.cathode, Q1.C, D2.cathode, C2.+, C3.+, C4.+
  N5: R1.Pin_1, U2.C, Q1.B
  N6: Q1.E, J1.pin2
