# Fritzing sketch Sensor_Fluxo_Agua (saved by Fritzing 0.9.3b)

parts:
  Raspberry_Pi1 = Raspberry Pi B+
  YF-S201_Flow_Meter1 = YF-S201 Water Flow Meter

nets:
  3V3: Raspberry_Pi1.3v3, Raspberry_Pi1.3V3, YF-S201_Flow_Meter1.VCC
  GND: Raspberry_Pi1.GND, YF-S201_Flow_Meter1.GND
  N1: Raspberry_Pi1.GPIO22, YF-S201_Flow_Meter1.SIG

custom parts:
  YF-S201 Water Flow Meter: The YF-S201 Flow Meter. The input voltage is 5V to 24V (DC).
