# Fritzing sketch all_Sensor_Conection_MLX90614 (saved by Fritzing 0.9.3b)
circuit board: 8.46667cm x 5.64444cm

parts:
  U1 = MLX90614 [package=to-39]
  U2 = MLX90614 [package=to-39]
  U3 = MLX90614 [package=to-39]
  J2 = female pin header, 4 pins [form="♀ (female)"]
  Raspberry_Pi_3_B+ = Raspberry Pi B+
  YF-S201_Flow_Meter1 = YF-S201 Water Flow Meter
  YF-S201_Flow_Meter2 = YF-S201 Water Flow Meter
  YF-S201_Flow_Meter3 = YF-S201 Water Flow Meter
  U4 = MLX90614 [package=to-39]
  Circuito_Acionamento_Rele_9 = IC, DIP package, 6 pins [chip_label=IC]
  Circuito_Acionamento_Rele_10 = IC, DIP package, 6 pins [chip_label=IC]
  Circuito_Acionamento_Rele_11 = IC, DIP package, 6 pins [chip_label=IC]
  Circuito_Acionamento_Rele_12 = IC, DIP package, 6 pins [chip_label=IC]
  Circuito_Acionamento_Rele_13 = IC, DIP package, 6 pins [chip_label=IC]
  Circuito_Acionamento_Rele_14 = IC, DIP package, 6 pins [chip_label=IC]
  Circuito_Acionamento_Rele_15 = IC, DIP package, 6 pins [chip_label=IC]
  Circuito_Acionamento_Rele_1 = IC, DIP package, 6 pins [chip_label=IC]
  Circuito_Acionamento_Rele_2 = IC, DIP package, 6 pins [chip_label=IC]
  Circuito_Acionamento_Rele_7 = IC, DIP package, 6 pins [chip_label=IC]
  Circuito_Acionamento_Rele_4 = IC, DIP package, 6 pins [chip_label=IC]
  Circuito_Acionamento_Rele_5 = IC, DIP package, 6 pins [chip_label=IC]
  Circuito_Acionamento_Rele_3 = IC, DIP package, 6 pins [chip_label=IC]
  Circuito_Acionamento_Rele_6 = IC, DIP package, 6 pins [chip_label=IC]
  Motor_Insumos_1 = Basic Servo
  Motor_Insumos_2 = Basic Servo
  Motor_Insumos_3 = Basic Servo
  Motor_Insumos_4 = Basic Servo
  Motor_Insumos_5 = Basic Servo
  Nobreak = AC Power [voltage=220V frequency=60]
  Resistencia_1 = Resistor [tolerance=±5% resistance=4k package=THT]
  Resistencia_2 = Resistor [tolerance=±5% resistance=4k package=THT]
  Resistencia_3 = Resistor [tolerance=±5% resistance=4k package=THT]
  Válvula_1 = Solenoid
  Válvula_2 = Solenoid
  Válvula_3 = Solenoid
  Válvula_4 = Solenoid
  Válvula_6 = Solenoid
  Válvula_7 = Solenoid
  Válvula_8 = Solenoid
  Válvula_9 = Solenoid
  Bomba_D'gua_1 = Vibration Motor- ROB-08449 [package=vibe-motor-10mm]
  Bomba_D'gua_2 = Vibration Motor- ROB-08449 [package=vibe-motor-10mm]
  Peltier_1 = Peltier Element
  Peltier_2 = Peltier Element
  Peltier_3 = Peltier Element
  Fonte_Peltier = DC Power [voltage=12V]
  Ventoinha_1 = Fan - Ventilador [package=THT]
  Ventoinha_2 = Fan - Ventilador [package=THT]
  Ventoinha_3 = Fan - Ventilador [package=THT]
  Circuito_Acionamento_Rele_8 = IC, DIP package, 6 pins [chip_label=IC]
  Válvula_5 = Solenoid

nets:
  N1: U1.SCL_VZ, U2.SCL_VZ, U3.SCL_VZ, J2.pin3, Raspberry_Pi_3_B+.GPIO3, U4.SCL_VZ
  N2: U1.PWM_SDA, U2.PWM_SDA, U3.PWM_SDA, J2.pin4, Raspberry_Pi_3_B+.GPIO2, U4.PWM_SDA
  VDD: U1.VDD, U2.VDD, U3.VDD, J2.pin1, Raspberry_Pi_3_B+.3v3, U4.VDD
  GND: U1.VSS, U2.VSS, U3.VSS, J2.pin2, Raspberry_Pi_3_B+.GND, YF-S201_Flow_Meter1.GND, YF-S201_Flow_Meter2.GND, YF-S201_Flow_Meter3.GND, U4.VSS, Circuito_Acionamento_Rele_9.pin3, Circuito_Acionamento_Rele_10.pin3, Circuito_Acionamento_Rele_11.pin3, Circuito_Acionamento_Rele_12.pin3, Circuito_Acionamento_Rele_13.pin3, Circuito_Acionamento_Rele_14.pin3, Circuito_Acionamento_Rele_15.pin3, Circuito_Acionamento_Rele_1.pin3, Circuito_Acionamento_Rele_2.pin3, Circuito_Acionamento_Rele_7.pin3, Circuito_Acionamento_Rele_4.pin3, Circuito_Acionamento_Rele_5.pin3, Circuito_Acionamento_Rele_3.pin3, Circuito_Acionamento_Rele_6.pin3, Motor_Insumos_1.gnd, Motor_Insumos_2.gnd, Motor_Insumos_3.gnd, Motor_Insumos_4.gnd, Motor_Insumos_5.gnd, Circuito_Acionamento_Rele_8.pin3
  N3: Raspberry_Pi_3_B+.GPIO4, Motor_Insumos_1.pulse, Motor_Insumos_2.pulse, Motor_Insumos_3.pulse, Motor_Insumos_4.pulse, Motor_Insumos_5.pulse
  N4: Raspberry_Pi_3_B+.GPIO17, YF-S201_Flow_Meter1.SIG, YF-S201_Flow_Meter2.SIG, YF-S201_Flow_Meter3.SIG
  N5: Raspberry_Pi_3_B+.GPIO27, Circuito_Acionamento_Rele_10.pin1
  N6: Raspberry_Pi_3_B+.GPIO22, Circuito_Acionamento_Rele_11.pin1
  N7: Raspberry_Pi_3_B+.GPIO10, Circuito_Acionamento_Rele_14.pin1
  N8: Raspberry_Pi_3_B+.GPIO9, Circuito_Acionamento_Rele_15.pin1
  N9: Raspberry_Pi_3_B+.GPIO11, Circuito_Acionamento_Rele_6.pin1
  N10: Raspberry_Pi_3_B+.GPIO5, Circuito_Acionamento_Rele_3.pin1
  N11: Raspberry_Pi_3_B+.GPIO6, Circuito_Acionamento_Rele_2.pin1
  N12: Raspberry_Pi_3_B+.GPIO13, Circuito_Acionamento_Rele_8.pin1
  N13: Raspberry_Pi_3_B+.GPIO12, Circuito_Acionamento_Rele_1.pin1
  N14: Raspberry_Pi_3_B+.GPIO7, Circuito_Acionamento_Rele_4.pin1
  N15: Raspberry_Pi_3_B+.GPIO8, Circuito_Acionamento_Rele_5.pin1
  N16: Raspberry_Pi_3_B+.GPIO25, Circuito_Acionamento_Rele_7.pin1
  N17: Raspberry_Pi_3_B+.GPIO24, Circuito_Acionamento_Rele_13.pin1
  N18: Raspberry_Pi_3_B+.GPIO23, Circuito_Acionamento_Rele_12.pin1
  N19: Raspberry_Pi_3_B+.GPIO18, Circuito_Acionamento_Rele_9.pin1
  VCC: Raspberry_Pi_3_B+.5V, YF-S201_Flow_Meter1.VCC, YF-S201_Flow_Meter2.VCC, YF-S201_Flow_Meter3.VCC, Circuito_Acionamento_Rele_9.pin2, Circuito_Acionamento_Rele_10.pin2, Circuito_Acionamento_Rele_11.pin2, Circuito_Acionamento_Rele_12.pin2, Circuito_Acionamento_Rele_13.pin2, Circuito_Acionamento_Rele_14.pin2, Circuito_Acionamento_Rele_15.pin2, Circuito_Acionamento_Rele_1.pin2, Circuito_Acionamento_Rele_2.pin2, Circuito_Acionamento_Rele_7.pin2, Circuito_Acionamento_Rele_4.pin2, Circuito_Acionamento_Rele_5.pin2, Circuito_Acionamento_Rele_3.pin2, Circuito_Acionamento_Rele_6.pin2, Motor_Insumos_1.vcc, Motor_Insumos_2.vcc, Motor_Insumos_3.vcc, Motor_Insumos_4.vcc, Motor_Insumos_5.vcc, Circuito_Acionamento_Rele_8.pin2
  N20: Circuito_Acionamento_Rele_9.pin5, Válvula_4.pin1
  N21: Circuito_Acionamento_Rele_9.pin6, Circuito_Acionamento_Rele_10.pin6, Circuito_Acionamento_Rele_11.pin6, Circuito_Acionamento_Rele_12.pin6, Circuito_Acionamento_Rele_13.pin6, Circuito_Acionamento_Rele_14.pin6, Circuito_Acionamento_Rele_15.pin6, Circuito_Acionamento_Rele_2.pin6, Circuito_Acionamento_Rele_7.pin6, Circuito_Acionamento_Rele_4.pin6, Circuito_Acionamento_Rele_5.pin6, Circuito_Acionamento_Rele_3.pin6, Circuito_Acionamento_Rele_6.pin6, Nobreak.V+, Circuito_Acionamento_Rele_8.pin6
  N22: Circuito_Acionamento_Rele_10.pin5, Válvula_3.pin1
  N23: Circuito_Acionamento_Rele_11.pin5, Válvula_2.pin1
  N24: Circuito_Acionamento_Rele_12.pin5, Válvula_1.pin1
  N25: Circuito_Acionamento_Rele_13.pin5, Resistencia_2.Pin_0
  N26: Circuito_Acionamento_Rele_14.pin5, Resistencia_3.Pin_0
  N27: Circuito_Acionamento_Rele_15.pin5, Resistencia_1.Pin_0
  GND_2: Circuito_Acionamento_Rele_1.pin5, Peltier_1.pin2, Peltier_2.pin2, Peltier_3.pin2, Ventoinha_1.GND, Ventoinha_2.GND, Ventoinha_3.GND
  N28: Circuito_Acionamento_Rele_1.pin6, Fonte_Peltier.V-
  N29: Circuito_Acionamento_Rele_2.pin5, Bomba_D'gua_2.-
  N30: Circuito_Acionamento_Rele_7.pin5, Válvula_6.pin1
  N31: Circuito_Acionamento_Rele_4.pin5, Válvula_9.pin1
  N32: Circuito_Acionamento_Rele_5.pin5, Válvula_8.pin1
  N33: Circuito_Acionamento_Rele_3.pin5, Bomba_D'gua_1.-
  N34: Circuito_Acionamento_Rele_6.pin5, Válvula_7.pin1
  N35: Nobreak.V-, Resistencia_1.Pin_1, Resistencia_2.Pin_1, Resistencia_3.Pin_1, Válvula_1.pin2, Válvula_2.pin2, Válvula_3.pin2, Válvula_4.pin2, Válvula_6.pin2, Válvula_7.pin2, Válvula_8.pin2, Válvula_9.pin2, Bomba_D'gua_1.+, Bomba_D'gua_2.+, Válvula_5.pin2
  5V: Peltier_1.pin1, Peltier_2.pin1, Peltier_3.pin1, Fonte_Peltier.V+, Ventoinha_1.5V, Ventoinha_2.5V, Ventoinha_3.5V
  N36: Circuito_Acionamento_Rele_8.pin5, Válvula_5.pin1

custom parts:
  YF-S201 Water Flow Meter: The YF-S201 Flow Meter. The input voltage is 5V to 24V (DC).
  Fan - Ventilador: Ventilador de 2 pines, se encuentra comunmente en computadoras de escritorio
