# Fritzing sketch sensor_fluxo (saved by Fritzing 0.9.3b)
breadboards: 1

parts:
  Raspberry_Pi_1 = Raspberry Pi 3 [part_number=RPI-3-V1.2]
  U1 = HALL-EFFECT [package=sc70]

nets:
  GND: Raspberry_Pi_1.GND, U1.GND
  5V: Raspberry_Pi_1.5V, U1.VCC
